# Fritzing sketch squirlrob_schematic (saved by Fritzing 0.9.3b)

parts:
  Part2 = Bluetooth HC-06
  Part3 = Arduino Pro Mini v13
  VCC1 = 4 x AAA Battery Mount
  J2 = Basic Servo
  J3 = Basic Servo

nets:
  N1: Part2.RXD, Part3.D0/TX
  N2: Part2.TXD, Part3.D1/RX
  GND: Part2.GND, Part3.GND, VCC1.-, J2.gnd, J3.gnd
  VCC: Part2.VCC, Part3.RAW, VCC1.+, J2.vcc, J3.vcc
  N3: Part3.D11_PWM/MOSI, J3.pulse
  N4: Part3.D10_PWM/SS, J2.pulse
